// Logisim project 1607045_1607023.circ as structural Verilog: 16 circuits, main circuit main
module main (
  input  CLR,
  input  Load,
  output [3:0] High,
  output [3:0] Low,
  output out_5,
  output High_2,
  output out_7,
  output out_8,
  output out_9,
  output out_10,
  output out_11,
  output out_12
);

  wire clock_1_out, controlled_buffer_1_out, controlled_buffer_6_out, CONTROLLER_cp, CONTROLLER_ea,
       CONTROLLER_ep, CONTROLLER_eu, CONTROLLER_hlt, CONTROLLER_nce, CONTROLLER_nel, CONTROLLER_nla,
       CONTROLLER_nlb, CONTROLLER_nll, CONTROLLER_nlm, CONTROLLER_nlo, CONTROLLER_su, not_1_out, not_2_out,
       not_3_out, not_4_out, not_5_out, not_6_out, not_7_out, not_8_out;
  wire [3:0] MAR_y0, PC_output;
  wire [7:0] Adder_Sub_out, bit_extender_1_out, IR_y0, REG_A_y, REG_B_y, xor_1_out;

  Program_Counter PC (.Clock(controlled_buffer_1_out), .Clear(CLR), .Output(PC_output));
  assign controlled_buffer_1_out = CONTROLLER_cp ? controlled_buffer_6_out : 1'bz;  // Controlled_Buffer controlled_buffer_1
  not not_1 (not_1_out, CONTROLLER_nlm);
  not not_2 (not_2_out, CONTROLLER_nce);
  _4_Bit_Reg MAR (
    .X3(Low[3]), .X2(Low[2]), .X1(Low[1]), .X0(Low[0]), .Y3(MAR_y0[3]), .Y2(MAR_y0[2]), .Y1(MAR_y0[1]),
    .Y0(MAR_y0[0]), .Load(not_1_out), .Clock(controlled_buffer_6_out), .Clear(CLR), .Enable(Load));
  not not_3 (not_3_out, CONTROLLER_nll);
  Controller CONTROLLER (
    .Ep(CONTROLLER_ep), .Cp(CONTROLLER_cp), .I7(IR_y0[7]), .I6(IR_y0[6]), .I5(IR_y0[5]), .I4(IR_y0[4]),
    .Clock(controlled_buffer_6_out), .HLT(CONTROLLER_hlt), .Clear(CLR), .nLm(CONTROLLER_nlm),
    .nCE(CONTROLLER_nce), .nEl(CONTROLLER_nel), .nLa(CONTROLLER_nla), .Ea(CONTROLLER_ea), .Su(CONTROLLER_su),
    .Eu(CONTROLLER_eu), .nLb(CONTROLLER_nlb), .nLo(CONTROLLER_nlo), .nLl(CONTROLLER_nll));
  assign Low = CONTROLLER_ep ? PC_output : 4'bz;  // Controlled_Buffer controlled_buffer_2
  _8_Bit_Reg IR (
    .X7(High[3]), .X6(High[2]), .X5(High[1]), .X4(High[0]), .X3(Low[3]), .X2(Low[2]), .X1(Low[1]),
    .X0(Low[0]), .Y7(IR_y0[7]), .Y6(IR_y0[6]), .Y5(IR_y0[5]), .Y4(IR_y0[4]), .Y3(IR_y0[3]), .Y2(IR_y0[2]),
    .Y1(IR_y0[1]), .Y0(IR_y0[0]), .Load(not_3_out), .Clock(controlled_buffer_6_out), .Clear(CLR));
  RAM #(.addrWidth(4)) ram_1 (.addr(MAR_y0), .data({High, Low}), .ld(not_2_out));  // open: sel, clk, clr
  assign Low = not_4_out ? IR_y0[3:0] : 4'bz;  // Controlled_Buffer controlled_buffer_3
  not not_4 (not_4_out, CONTROLLER_nel);
  assign {High, Low} = CONTROLLER_ea ? REG_A_y : 8'bz;  // Controlled_Buffer controlled_buffer_4
  not not_5 (not_5_out, CONTROLLER_hlt);
  assign {High, Low} = CONTROLLER_eu ? Adder_Sub_out : 8'bz;  // Controlled_Buffer controlled_buffer_5
  Clock clock_1 (.out(clock_1_out));
  assign controlled_buffer_6_out = not_5_out ? clock_1_out : 1'bz;  // Controlled_Buffer controlled_buffer_6
  not not_6 (not_6_out, CONTROLLER_nlb);
  Buffer_Register_1607045 REG_A (
    .X({High, Low}), .Load(not_8_out), .clock(controlled_buffer_6_out), .Clear(CLR), .Y(REG_A_y));
  ADD_SUB_1607045 Adder_Sub (.A(REG_A_y), .B(xor_1_out), .Cin(CONTROLLER_su), .OUT(Adder_Sub_out));  // open: COUT
  assign xor_1_out = REG_B_y ^ bit_extender_1_out;  // XOR_Gate xor_1, 8 bits wide
  Buffer_Register_1607045 REG_B (
    .X({High, Low}), .Load(not_6_out), .clock(controlled_buffer_6_out), .Clear(CLR), .Y(REG_B_y));
  Buffer_Register_1607045 OUT (
    .X({High, Low}), .Load(not_7_out), .clock(controlled_buffer_6_out), .Clear(CLR),
    .Y({out_12, out_11, out_10, out_9, out_8, out_7, High_2, out_5}));
  not not_7 (not_7_out, CONTROLLER_nlo);
  assign bit_extender_1_out = {{7{CONTROLLER_su}}, CONTROLLER_su};  // Bit_Extender bit_extender_1
  not not_8 (not_8_out, CONTROLLER_nla);
  Hex_Digit_Display hex_digit_display_1 (.value({out_12, out_11, out_10, out_9}));  // open: dp
  Hex_Digit_Display hex_digit_display_2 (.value({out_8, out_7, High_2, out_5}));  // open: dp

  // Notes on the sheet:
  //   1607023
  //   RAM
  //   1607045
  //   Low
endmodule

module Program_Counter (
  input  Clock,
  input  Clear,
  output [3:0] Output
);

  wire and_1_out, and_2_out;

  J_K_Flip_Flop j_k_ff_1 (.J(1'b1), .clk(Clock), .K(1'b1), .Q(Output[0]), .reset(Clear));  // open: Qn, preset, en
  and and_1 (and_1_out, Output[0], Output[1]);
  J_K_Flip_Flop j_k_ff_2 (
    .J(Output[0]), .clk(Clock), .K(Output[0]), .Q(Output[1]), .reset(Clear));  // open: Qn, preset, en
  J_K_Flip_Flop j_k_ff_3 (
    .J(and_1_out), .clk(Clock), .K(and_1_out), .Q(Output[2]), .reset(Clear));  // open: Qn, preset, en
  and and_2 (and_2_out, Output[0], Output[1], Output[2]);
  J_K_Flip_Flop j_k_ff_4 (
    .J(and_2_out), .clk(Clock), .K(and_2_out), .Q(Output[3]), .reset(Clear));  // open: Qn, preset, en

  // Notes on the sheet:
  //   1607023
  //   Constant
endmodule

// Rep
module Repeater (
  input  Load,
  input  Xi,
  input  SQ,
  output out
);

  wire and_1_out, and_2_out, NOT_out;

  not NOT (NOT_out, Load);
  and and_1 (and_1_out, Load, Xi);
  and and_2 (and_2_out, NOT_out, SQ);
  or or_1 (out, and_1_out, and_2_out);

  // Notes on the sheet:
  //   1607023
endmodule

module _4_Bit_Reg (
  input  Load,
  input  X1,
  input  X0,
  input  X2,
  input  X3,
  input  Clock,
  input  Clear,
  input  Enable,
  output Y3,
  output Y2,
  output Y1,
  output Y0
);

  wire D0_q, D1_q, D2_q, D3_q, repeater_1_out, repeater_2_out, repeater_3_out, repeater_4_out;

  Repeater repeater_1 (.Load(Load), .Xi(X3), .SQ(D3_q), .out(repeater_1_out));
  D_Flip_Flop D3 (.clk(Clock), .D(repeater_1_out), .Q(D3_q), .reset(Clear));  // open: Qn, preset, en
  assign Y3 = Enable ? D3_q : 1'bz;  // Controlled_Buffer _3
  Repeater repeater_2 (.Load(Load), .Xi(X2), .SQ(D2_q), .out(repeater_2_out));
  D_Flip_Flop D2 (.clk(Clock), .D(repeater_2_out), .Q(D2_q), .reset(Clear));  // open: Qn, preset, en
  assign Y2 = Enable ? D2_q : 1'bz;  // Controlled_Buffer _2
  Repeater repeater_3 (.Load(Load), .Xi(X1), .SQ(D1_q), .out(repeater_3_out));
  D_Flip_Flop D1 (.clk(Clock), .D(repeater_3_out), .Q(D1_q), .reset(Clear));  // open: Qn, preset, en
  assign Y1 = Enable ? D1_q : 1'bz;  // Controlled_Buffer _1
  Repeater repeater_4 (.Load(Load), .Xi(X0), .SQ(D0_q), .out(repeater_4_out));
  D_Flip_Flop D0 (.clk(Clock), .D(repeater_4_out), .Q(D0_q), .reset(Clear));  // open: Qn, preset, en
  assign Y0 = Enable ? D0_q : 1'bz;  // Controlled_Buffer _0

  // Notes on the sheet:
  //   1607023
endmodule

module _8_Bit_Reg (
  input  Load,
  input  X1,
  input  X0,
  input  X5,
  input  X4,
  input  X2,
  input  X6,
  input  X3,
  input  X7,
  input  Clock,
  input  Clear,
  output Y1,
  output Y0,
  output Y7,
  output Y6,
  output Y5,
  output Y4,
  output Y3,
  output Y2
);

  wire repeater_1_out, repeater_2_out, repeater_3_out, repeater_4_out, repeater_5_out, repeater_6_out,
       repeater_7_out, repeater_8_out;

  Repeater repeater_1 (.Load(Load), .Xi(X7), .SQ(Y7), .out(repeater_1_out));
  D_Flip_Flop D7 (.clk(Clock), .D(repeater_1_out), .Q(Y7), .reset(Clear));  // open: Qn, preset, en
  Repeater repeater_2 (.Load(Load), .Xi(X6), .SQ(Y6), .out(repeater_2_out));
  D_Flip_Flop D6 (.clk(Clock), .D(repeater_2_out), .Q(Y6), .reset(Clear));  // open: Qn, preset, en
  Repeater repeater_3 (.Load(Load), .Xi(X5), .SQ(Y5), .out(repeater_3_out));
  D_Flip_Flop D5 (.clk(Clock), .D(repeater_3_out), .Q(Y5), .reset(Clear));  // open: Qn, preset, en
  Repeater repeater_4 (.Load(Load), .Xi(X4), .SQ(Y4), .out(repeater_4_out));
  D_Flip_Flop D4 (.clk(Clock), .D(repeater_4_out), .Q(Y4), .reset(Clear));  // open: Qn, preset, en
  Repeater repeater_5 (.Load(Load), .Xi(X3), .SQ(Y3), .out(repeater_5_out));
  D_Flip_Flop D3 (.clk(Clock), .D(repeater_5_out), .Q(Y3), .reset(Clear));  // open: Qn, preset, en
  Repeater repeater_6 (.Load(Load), .Xi(X2), .SQ(Y2), .out(repeater_6_out));
  D_Flip_Flop D2 (.clk(Clock), .D(repeater_6_out), .Q(Y2), .reset(Clear));  // open: Qn, preset, en
  Repeater repeater_7 (.Load(Load), .Xi(X1), .SQ(Y1), .out(repeater_7_out));
  D_Flip_Flop D1 (.clk(Clock), .D(repeater_7_out), .Q(Y1), .reset(Clear));  // open: Qn, preset, en
  Repeater repeater_8 (.Load(Load), .Xi(X0), .SQ(Y0), .out(repeater_8_out));
  D_Flip_Flop D0 (.clk(Clock), .D(repeater_8_out), .Q(Y0), .reset(Clear));  // open: Qn, preset, en

  // Notes on the sheet:
  //   1607023
endmodule

module c39 (
  input  _1,
  input  _4,
  input  _9,
  input  _10,
  input  _13,
  input  _12,
  output _3,
  output _6,
  output _8,
  output _11
);

  and and_1 (_3, _1, _10);
  and and_2 (_6, _4, _10);
  and and_3 (_8, _9, _10);
  and and_4 (_11, _12, _13);

  // Notes on the sheet:
  //   1607023
endmodule

module c40 (
  input  _9,
  input  _1,
  input  _4,
  input  _5,
  input  _12,
  input  _13,
  output _3,
  output _6,
  output _8,
  output _11
);

  and and_1 (_6, _4, _5);
  and and_2 (_3, _1, _5);
  and and_3 (_8, _9, _13);
  and and_4 (_11, _12, _13);

  // Notes on the sheet:
  //   1607023
endmodule

module c41 (
  input  _4,
  input  _5,
  input  _12,
  input  _13,
  input  _1,
  input  _2,
  input  _9,
  output _3,
  output _6,
  output _8,
  output _11
);

  and and_1 (_3, _1, _2);
  and and_2 (_8, _9, _13);
  and and_3 (_6, _4, _5);
  and and_4 (_11, _12, _13);

  // Notes on the sheet:
  //   1607023
endmodule

module c43 (
  input  _1,
  input  _4,
  input  _5,
  input  _9,
  input  _10,
  output _3,
  output _6,
  output _8
);

  and and_1 (_3, _1, _5);
  and and_2 (_8, _9, _10);
  and and_3 (_6, _4, _5);

  // Notes on the sheet:
  //   1607023
endmodule

module Ring_Counter_1607045 (
  input  Clock,
  input  CLEAR,
  output T2,
  output T3,
  output T1,
  output T4,
  output T5,
  output T6
);

  wire j_k_ff_1_q, j_k_ff_2_qn, j_k_ff_3_qn, j_k_ff_4_qn, j_k_ff_5_qn, j_k_ff_6_qn;

  J_K_Flip_Flop j_k_ff_1 (
    .J(j_k_ff_6_qn), .clk(Clock), .K(T6), .Q(j_k_ff_1_q), .Qn(T1), .reset(CLEAR));  // open: preset, en
  J_K_Flip_Flop j_k_ff_2 (
    .J(T1), .clk(Clock), .K(j_k_ff_1_q), .Q(T2), .Qn(j_k_ff_2_qn), .reset(CLEAR));  // open: preset, en
  J_K_Flip_Flop j_k_ff_3 (
    .J(T2), .clk(Clock), .K(j_k_ff_2_qn), .Q(T3), .Qn(j_k_ff_3_qn), .reset(CLEAR));  // open: preset, en
  J_K_Flip_Flop j_k_ff_4 (
    .J(T3), .clk(Clock), .K(j_k_ff_3_qn), .Q(T4), .Qn(j_k_ff_4_qn), .reset(CLEAR));  // open: preset, en
  J_K_Flip_Flop j_k_ff_5 (
    .J(T4), .clk(Clock), .K(j_k_ff_4_qn), .Q(T5), .Qn(j_k_ff_5_qn), .reset(CLEAR));  // open: preset, en
  J_K_Flip_Flop j_k_ff_6 (
    .J(T5), .clk(Clock), .K(j_k_ff_5_qn), .Q(T6), .Qn(j_k_ff_6_qn), .reset(CLEAR));  // open: preset, en

  // Notes on the sheet:
  //   1607045
endmodule

module Decode_1607045 (
  input  l7,
  input  l6,
  input  l5,
  input  l4,
  output LDA,
  output ADD,
  output SUB,
  output OUT,
  output HLT
);

  wire and_1_out, and_2_out, and_3_out, and_4_out, and_5_out, not_1_out, not_2_out, not_3_out, not_4_out;

  not not_1 (not_1_out, l7);
  not not_2 (not_2_out, l6);
  not not_3 (not_3_out, l5);
  not not_4 (not_4_out, l4);
  and and_1 (and_1_out, not_1_out, not_2_out, not_3_out, not_4_out);
  and and_2 (and_2_out, not_1_out, not_2_out, not_3_out, l4);
  and and_3 (and_3_out, not_1_out, not_2_out, l5, not_4_out);
  and and_4 (and_4_out, l7, l6, l5, not_4_out);
  and and_5 (and_5_out, l7, l6, l5, l4);
  buf buffer_1 (LDA, and_1_out);
  buf buffer_2 (ADD, and_2_out);
  buf buffer_3 (SUB, and_3_out);
  buf buffer_4 (OUT, and_4_out);
  buf buffer_5 (HLT, and_5_out);

  // Notes on the sheet:
  //   1607045
endmodule

module Full_Adder_1607045 (
  input  A,
  input  B,
  input  Cin,
  output Cout,
  output S
);

  wire and_1_out, and_2_out, xor_1_out;

  xor xor_1 (xor_1_out, A, B);
  and and_1 (and_1_out, A, B);
  and and_2 (and_2_out, xor_1_out, Cin);
  xor xor_2 (S, xor_1_out, Cin);
  or or_1 (Cout, and_2_out, and_1_out);

  // Notes on the sheet:
  //   1607045
endmodule

// Repeater
module Repeater_1607045 (
  input  Load,
  input  Xi,
  input  S,
  output Yi
);

  wire AND_2_out, AND_out, NOT_out;

  not NOT (NOT_out, Load);
  and AND (AND_out, Load, Xi);
  and AND_2 (AND_2_out, NOT_out, S);
  or OR (Yi, AND_out, AND_2_out);

  // Notes on the sheet:
  //   1607045
endmodule

module Buffer_Register_1607045 (
  input  [7:0] X,
  input  Load,
  input  clock,
  input  Clear,
  output [7:0] Y
);

  wire repeater_1607045_1_yi, repeater_1607045_2_yi, repeater_1607045_3_yi, repeater_1607045_4_yi,
       repeater_1607045_5_yi, repeater_1607045_6_yi, repeater_1607045_7_yi, repeater_1607045_8_yi;

  Repeater_1607045 repeater_1607045_1 (.Load(Load), .Xi(X[7]), .S(Y[7]), .Yi(repeater_1607045_1_yi));
  D_Flip_Flop D7 (.clk(clock), .D(repeater_1607045_1_yi), .Q(Y[7]), .reset(Clear));  // open: Qn, preset, en
  Repeater_1607045 repeater_1607045_2 (.Load(Load), .Xi(X[6]), .S(Y[6]), .Yi(repeater_1607045_2_yi));
  D_Flip_Flop D6 (.clk(clock), .D(repeater_1607045_2_yi), .Q(Y[6]), .reset(Clear));  // open: Qn, preset, en
  Repeater_1607045 repeater_1607045_3 (.Load(Load), .Xi(X[5]), .S(Y[5]), .Yi(repeater_1607045_3_yi));
  D_Flip_Flop D5 (.clk(clock), .D(repeater_1607045_3_yi), .Q(Y[5]), .reset(Clear));  // open: Qn, preset, en
  Repeater_1607045 repeater_1607045_4 (.Load(Load), .Xi(X[4]), .S(Y[4]), .Yi(repeater_1607045_4_yi));
  D_Flip_Flop D4 (.clk(clock), .D(repeater_1607045_4_yi), .Q(Y[4]), .reset(Clear));  // open: Qn, preset, en
  Repeater_1607045 repeater_1607045_5 (.Load(Load), .Xi(X[3]), .S(Y[3]), .Yi(repeater_1607045_5_yi));
  D_Flip_Flop D3 (.clk(clock), .D(repeater_1607045_5_yi), .Q(Y[3]), .reset(Clear));  // open: Qn, preset, en
  Repeater_1607045 repeater_1607045_6 (.Load(Load), .Xi(X[2]), .S(Y[2]), .Yi(repeater_1607045_6_yi));
  D_Flip_Flop D2 (.clk(clock), .D(repeater_1607045_6_yi), .Q(Y[2]), .reset(Clear));  // open: Qn, preset, en
  Repeater_1607045 repeater_1607045_7 (.Load(Load), .Xi(X[1]), .S(Y[1]), .Yi(repeater_1607045_7_yi));
  D_Flip_Flop D1 (.clk(clock), .D(repeater_1607045_7_yi), .Q(Y[1]), .reset(Clear));  // open: Qn, preset, en
  Repeater_1607045 repeater_1607045_8 (.Load(Load), .Xi(X[0]), .S(Y[0]), .Yi(repeater_1607045_8_yi));
  D_Flip_Flop D0 (.clk(clock), .D(repeater_1607045_8_yi), .Q(Y[0]), .reset(Clear));  // open: Qn, preset, en

  // Notes on the sheet:
  //   1607045
endmodule

module ADD_SUB_1607045 (
  input  [7:0] A,
  input  [7:0] B,
  input  Cin,
  output COUT,
  output [7:0] OUT
);

  wire full_adder_1607045_1_cout, full_adder_1607045_2_cout, full_adder_1607045_3_cout,
       full_adder_1607045_4_cout, full_adder_1607045_5_cout, full_adder_1607045_6_cout,
       full_adder_1607045_7_cout;

  Full_Adder_1607045 full_adder_1607045_1 (.A(A[0]), .B(B[0]), .Cin(Cin), .Cout(full_adder_1607045_1_cout), .S(OUT[0]));
  Full_Adder_1607045 full_adder_1607045_2 (
    .A(A[1]), .B(B[1]), .Cin(full_adder_1607045_1_cout), .Cout(full_adder_1607045_2_cout), .S(OUT[1]));
  Full_Adder_1607045 full_adder_1607045_3 (
    .A(A[2]), .B(B[2]), .Cin(full_adder_1607045_2_cout), .Cout(full_adder_1607045_3_cout), .S(OUT[2]));
  Full_Adder_1607045 full_adder_1607045_4 (
    .A(A[3]), .B(B[3]), .Cin(full_adder_1607045_3_cout), .Cout(full_adder_1607045_4_cout), .S(OUT[3]));
  Full_Adder_1607045 full_adder_1607045_5 (
    .A(A[4]), .B(B[4]), .Cin(full_adder_1607045_4_cout), .Cout(full_adder_1607045_5_cout), .S(OUT[4]));
  Full_Adder_1607045 full_adder_1607045_6 (
    .A(A[5]), .B(B[5]), .Cin(full_adder_1607045_5_cout), .Cout(full_adder_1607045_6_cout), .S(OUT[5]));
  Full_Adder_1607045 full_adder_1607045_7 (
    .A(A[6]), .B(B[6]), .Cin(full_adder_1607045_6_cout), .Cout(full_adder_1607045_7_cout), .S(OUT[6]));
  Full_Adder_1607045 full_adder_1607045_8 (
    .A(A[7]), .B(B[7]), .Cin(full_adder_1607045_7_cout), .Cout(COUT), .S(OUT[7]));

  // Notes on the sheet:
  //   1607045
endmodule

module Controller (
  input  Clock,
  input  Clear,
  input  I7,
  input  I6,
  input  I5,
  input  I4,
  output Ep,
  output Cp,
  output HLT,
  output nLm,
  output nCE,
  output nEl,
  output nLa,
  output Ea,
  output Su,
  output Eu,
  output nLb,
  output nLo,
  output nLl
);

  wire c39__3, c39__6, c39__8, c39__11, c40__3, c40__6, c40__8, c40__11, c41_2__8, c41_2__11, c41__3, c41__6,
       c41__8, c41__11, c43__3, c43__6, c43__8, DC_add, DC_lda, DC_out, DC_sub, or_1_out, or_2_out, or_3_out,
       or_4_out, or_6_out, RC_t3, RC_t4, RC_t5, RC_t6;

  Decode_1607045 DC (
    .l7(I7), .l6(I6), .l5(I5), .l4(I4), .LDA(DC_lda), .ADD(DC_add), .SUB(DC_sub), .OUT(DC_out), .HLT(HLT));
  c39 c39 (
    ._1(DC_lda), ._4(DC_add), ._9(DC_sub), ._10(RC_t4), ._12(DC_lda), ._13(RC_t5), ._3(c39__3), ._6(c39__6),
    ._8(c39__8), ._11(c39__11));
  or or_1 (or_1_out, Ep, c39__3, c39__6, c39__8);
  not not_1 (nLm, or_1_out);
  Ring_Counter_1607045 RC (
    .Clock(Clock), .CLEAR(Clear), .T1(Ep), .T2(Cp), .T3(RC_t3), .T4(RC_t4), .T5(RC_t5), .T6(RC_t6));
  c40 c40 (
    ._1(DC_add), ._4(DC_sub), ._5(RC_t5), ._9(DC_lda), ._12(DC_add), ._13(RC_t4), ._3(c40__3), ._6(c40__6),
    ._8(c40__8), ._11(c40__11));
  or or_2 (or_2_out, c39__11, RC_t3, c40__3, c40__6);
  not not_2 (nCE, or_2_out);
  or or_3 (or_3_out, c40__8, c40__11, c41__3);
  not not_3 (nEl, or_3_out);
  c41 c41 (
    ._1(DC_sub), ._2(RC_t4), ._4(DC_lda), ._5(RC_t5), ._9(DC_add), ._12(DC_sub), ._13(RC_t6), ._3(c41__3),
    ._6(c41__6), ._8(c41__8), ._11(c41__11));
  or or_4 (or_4_out, c41__6, c41__8, c41__11);
  not not_4 (nLa, or_4_out);
  c41 c41_2 (
    ._1(DC_out), ._2(RC_t4), ._4(DC_sub), ._5(RC_t6), ._9(DC_add), ._12(DC_sub), ._13(RC_t6), ._3(Ea),
    ._6(Su), ._8(c41_2__8), ._11(c41_2__11));
  or or_5 (Eu, c41_2__8, c41_2__11);
  c43 c43 (._1(DC_add), ._4(DC_sub), ._5(RC_t5), ._9(DC_out), ._10(RC_t4), ._3(c43__3), ._6(c43__6), ._8(c43__8));
  or or_6 (or_6_out, c43__3, c43__6);
  not not_5 (nLb, or_6_out);
  not not_6 (nLo, c43__8);
  not not_7 (nLl, RC_t3);

  // Notes on the sheet:
  //   1607023
  //   T1
  //   T2
  //   T3
  //   T4
  //   T5
  //   T6
endmodule
